// Logisim project SPM.circ as structural Verilog: 3 circuits, main circuit main
module main (
  input  y__serial_in,
  input  x0,
  input  x1,
  input  x2,
  input  x3,
  input  x4,
  input  x5,
  input  x6,
  input  x7,
  input  in_10,
  output serial_output
);

  wire and_1_out, and_2_out, and_3_out, and_4_out, and_5_out, and_6_out, and_7_out, and_8_out, clock_1_out,
       csadd_2_sum, csadd_3_sum, csadd_4_sum, csadd_5_sum, csadd_6_sum, csadd_7_sum, tcmp_1_out_4;

  Clock clock_1 (.out(clock_1_out));
  and and_1 (and_1_out, x0, y__serial_in);
  and and_2 (and_2_out, x1, y__serial_in);
  and and_3 (and_3_out, x2, y__serial_in);
  and and_4 (and_4_out, x3, y__serial_in);
  and and_5 (and_5_out, x4, y__serial_in);
  and and_6 (and_6_out, x5, x5, y__serial_in);
  and and_7 (and_7_out, x6, y__serial_in);
  and and_8 (and_8_out, x7, y__serial_in);
  CSADD csadd_1 (.X(and_1_out), .Y(csadd_2_sum), .SUM(serial_output), .rst(in_10), .clk(clock_1_out));
  CSADD csadd_2 (.X(and_2_out), .Y(csadd_3_sum), .SUM(csadd_2_sum), .rst(in_10), .clk(clock_1_out));
  CSADD csadd_3 (.X(and_3_out), .Y(csadd_4_sum), .SUM(csadd_3_sum), .rst(in_10), .clk(clock_1_out));
  CSADD csadd_4 (.X(and_4_out), .Y(csadd_5_sum), .SUM(csadd_4_sum), .rst(in_10), .clk(clock_1_out));
  CSADD csadd_5 (.X(and_5_out), .Y(csadd_6_sum), .SUM(csadd_5_sum), .rst(in_10), .clk(clock_1_out));
  CSADD csadd_6 (.X(and_6_out), .Y(csadd_7_sum), .SUM(csadd_6_sum), .rst(in_10), .clk(clock_1_out));
  CSADD csadd_7 (.X(and_7_out), .Y(tcmp_1_out_4), .SUM(csadd_7_sum), .rst(in_10), .clk(clock_1_out));
  TCMP tcmp_1 (.A(and_8_out), .reset(in_10), .out_4(tcmp_1_out_4), .clk(clock_1_out));

  // Notes on the sheet:
  //   reset
  //   clk
endmodule

module CSADD (
  input  X,
  input  Y,
  input  clk,
  input  rst,
  output SUM
);

  wire adder_1_cout, adder_1_out, and_1_out, and_2_out, d_ff_2_q, not_1_out, xor_1_out, xor_2_out;

  Adder #(.width(1)) adder_1 (.a(Y), .b(d_ff_2_q), .out(adder_1_out), .cin(1'b0), .cout(adder_1_cout));
  not not_1 (not_1_out, rst);
  and and_1 (and_1_out, X, adder_1_out);
  xor xor_1 (xor_1_out, X, adder_1_out);
  D_Flip_Flop #(.trigger("high")) d_ff_1 (
    .clk(clk), .D(xor_1_out), .Q(SUM), .reset(not_1_out));  // open: Qn, preset, en
  and and_2 (and_2_out, and_1_out, adder_1_cout);
  xor xor_2 (xor_2_out, and_1_out, adder_1_cout);
  D_Flip_Flop #(.trigger("high")) d_ff_2 (
    .clk(clk), .D(xor_2_out), .Q(d_ff_2_q), .reset(not_1_out));  // open: Qn, preset, en

  // Notes on the sheet:
  //   FDHA
  //   HSUM1
  //   CAR1
  //   FDHA
  //   SC
endmodule

module TCMP (
  input  A,
  input  clk,
  input  reset,
  output out_4
);

  wire d_ff_2_q, FDHA_out, not_1_out, or_1_out, xor_1_out;

  not not_1 (not_1_out, reset);
  and FDHA (FDHA_out, A, d_ff_2_q);
  xor xor_1 (xor_1_out, A, d_ff_2_q);
  D_Flip_Flop #(.trigger("high")) d_ff_1 (
    .clk(clk), .D(xor_1_out), .Q(out_4), .reset(not_1_out));  // open: Qn, preset, en
  or or_1 (or_1_out, A, d_ff_2_q);
  D_Flip_Flop #(.trigger("high")) d_ff_2 (
    .clk(clk), .D(or_1_out), .Q(d_ff_2_q), .reset(not_1_out));  // open: Qn, preset, en
endmodule
